// Digital circuit Memoria_As2.dig as structural Verilog
module Memoria_As2 (
  input  [31:0] addr,
  input  [31:0] DataW,
  input  WE,
  input  [2:0] DMCtrl,
  input  clk,
  output [31:0] DataR
);

  wire _1A, _1E, _2E, _3A, _3E, _4E, and_2_out, and_3_out, and_4_out, and_5_out, and_6_out, and_7_out,
       and_8_out, and_9_out, not_1_out, not_2_out, or_2_out, or_3_out, or_4_out, or_5_out;
  wire [7:0] multiplexer_2_out, multiplexer_4_out, multiplexer_7_out, multiplexer_10_out, multiplexer_11_out,
       multiplexer_12_out, R1_q, R2_q, R3_q, R4_q;
  wire [15:0] multiplexer_6_out;
  wire [23:0] add_1_s, multiplexer_3_out, multiplexer_5_out, multiplexer_8_out;
  wire [31:0] barrelshifter_1_out, barrelshifter_2_out, bitextender_1_out, bitextender_2_out,
       multiplexer_1_out, notconnected_1_out, notconnected_2_out, notconnected_3_out, notconnected_4_out;

  or or_1 (_1A, addr[0], addr[1]);
  and and_1 (_3A, addr[0], addr[1]);
  not not_1 (not_1_out, addr[1]);
  BarrelShifter #(.Bits(32)) barrelshifter_1 (.in(DataW), .shift(6'b010000), .out(barrelshifter_1_out));
  BarrelShifter #(.Bits(32)) barrelshifter_2 (.in(DataW), .shift(6'b011000), .out(barrelshifter_2_out));
  not not_2 (not_2_out, addr[0]);
  and and_2 (and_2_out, not_2_out, not_1_out);
  and and_3 (and_3_out, addr[0], addr[1], DMCtrl[0]);
  and and_4 (and_4_out, addr[0], not_1_out);
  and and_5 (and_5_out, not_1_out, DMCtrl[0]);
  and and_6 (and_6_out, addr[0], not_1_out, DMCtrl[0]);
  and and_7 (and_7_out, not_2_out, addr[1]);
  and and_8 (and_8_out, addr[0], addr[1]);
  and and_9 (and_9_out, addr[1], DMCtrl[0]);
  Multiplexer #(.Bits(32), .Selector_Bits(2)) multiplexer_1 (
    .sel(DMCtrl[1:0]), .in_0(DataW), .in_1(barrelshifter_1_out), .in_2(barrelshifter_2_out),
    .in_3(notconnected_1_out), .out(multiplexer_1_out));
  // NotConnected on notconnected_1_out
  or or_2 (or_2_out, and_2_out, and_3_out, DMCtrl[1]);
  or or_3 (or_3_out, and_4_out, and_5_out, DMCtrl[1]);
  or or_4 (or_4_out, and_6_out, and_7_out, DMCtrl[1]);
  or or_5 (or_5_out, and_8_out, and_9_out, DMCtrl[1]);
  Add #(.Bits(24)) add_1 (.a(24'h1), .b(addr[25:2]), .c_i(1'b0), .s(add_1_s));  // open: c_o
  and and_10 (_1E, WE, or_2_out);
  and and_11 (_2E, WE, or_3_out);
  and and_12 (_3E, WE, or_4_out);
  and and_13 (_4E, WE, or_5_out);
  Multiplexer #(.Selector_Bits(2), .Bits(8)) multiplexer_2 (
    .sel(addr[1:0]), .in_0(multiplexer_1_out[31:24]), .in_1(multiplexer_1_out[7:0]),
    .in_2(multiplexer_1_out[15:8]), .in_3(multiplexer_1_out[23:16]), .out(multiplexer_2_out));
  RAMAsync #(.AddrBits(24), .Bits(8)) R1 (.A(multiplexer_3_out), .D(multiplexer_2_out), .we(_1E), .Q(R1_q));
  Multiplexer #(.Bits(24)) multiplexer_3 (.sel(_1A), .in_0(addr[25:2]), .in_1(add_1_s), .out(multiplexer_3_out));
  Multiplexer #(.Selector_Bits(2), .Bits(8)) multiplexer_4 (
    .sel(addr[1:0]), .in_0(multiplexer_1_out[23:16]), .in_1(multiplexer_1_out[31:24]),
    .in_2(multiplexer_1_out[7:0]), .in_3(multiplexer_1_out[15:8]), .out(multiplexer_4_out));
  Multiplexer #(.Bits(24)) multiplexer_5 (.sel(addr[1]), .in_0(addr[25:2]), .in_1(add_1_s), .out(multiplexer_5_out));
  RAMAsync #(.AddrBits(24), .Bits(8)) R2 (.A(multiplexer_5_out), .D(multiplexer_4_out), .we(_2E), .Q(R2_q));
  Multiplexer #(.Selector_Bits(2), .Bits(8)) multiplexer_6 (
    .sel(addr[1:0]), .in_0(R1_q), .in_1(R2_q), .in_2(R3_q), .in_3(R4_q), .out(multiplexer_6_out[15:8]));
  Multiplexer #(.Selector_Bits(2), .Bits(8)) multiplexer_7 (
    .sel(addr[1:0]), .in_0(multiplexer_1_out[15:8]), .in_1(multiplexer_1_out[23:16]),
    .in_2(multiplexer_1_out[31:24]), .in_3(multiplexer_1_out[7:0]), .out(multiplexer_7_out));
  Multiplexer #(.Bits(24)) multiplexer_8 (.sel(_3A), .in_0(addr[25:2]), .in_1(add_1_s), .out(multiplexer_8_out));
  RAMAsync #(.AddrBits(24), .Bits(8)) R3 (.A(multiplexer_8_out), .D(multiplexer_7_out), .we(_3E), .Q(R3_q));
  Multiplexer #(.Selector_Bits(2), .Bits(8)) multiplexer_9 (
    .sel(addr[1:0]), .in_0(R2_q), .in_1(R3_q), .in_2(R4_q), .in_3(R1_q), .out(multiplexer_6_out[7:0]));
  Multiplexer #(.Selector_Bits(2), .Bits(8)) multiplexer_10 (
    .sel(addr[1:0]), .in_0(R3_q), .in_1(R4_q), .in_2(R1_q), .in_3(R2_q), .out(multiplexer_10_out));
  Multiplexer #(.Selector_Bits(2), .Bits(8)) multiplexer_11 (
    .sel(addr[1:0]), .in_0(multiplexer_1_out[7:0]), .in_1(multiplexer_1_out[15:8]),
    .in_2(multiplexer_1_out[23:16]), .in_3(multiplexer_1_out[31:24]), .out(multiplexer_11_out));
  RAMAsync #(.AddrBits(24), .Bits(8)) R4 (.A(addr[25:2]), .D(multiplexer_11_out), .we(_4E), .Q(R4_q));
  Multiplexer #(.Selector_Bits(2), .Bits(8)) multiplexer_12 (
    .sel(addr[1:0]), .in_0(R4_q), .in_1(R1_q), .in_2(R2_q), .in_3(R3_q), .out(multiplexer_12_out));
  BitExtender #(.outputBits(32)) bitextender_1 (.in(multiplexer_6_out[15:8]), .out(bitextender_1_out));
  BitExtender #(.inputBits(16), .outputBits(32)) bitextender_2 (.in(multiplexer_6_out), .out(bitextender_2_out));
  Multiplexer #(.Selector_Bits(3), .Bits(32)) multiplexer_13 (
    .sel(DMCtrl), .in_0(bitextender_1_out), .in_1(bitextender_2_out),
    .in_2({multiplexer_6_out, multiplexer_10_out, multiplexer_12_out}), .in_3(notconnected_2_out),
    .in_4({{24{1'b0}}, multiplexer_6_out[15:8]}), .in_5({{16{1'b0}}, multiplexer_6_out}),
    .in_6(notconnected_3_out), .in_7(notconnected_4_out), .out(DataR));
  // NotConnected on notconnected_2_out
  // NotConnected on notconnected_3_out
  // NotConnected on notconnected_4_out

  // Other names for the same wires on the sheet: _2A = addr[1]
endmodule
