// Digital circuit InsMem.dig as structural Verilog
module InsMem (
  input  [25:0] Da,
  output [31:0] Instr
);

  wire [7:0] M1_d, M2_d, M3_d, M4_d;

  ROM #(.AddrBits(24), .Bits(8)) M1 (.A(Da[25:2]), .sel(1'b1), .D(M1_d));
  ROM #(.AddrBits(24), .Bits(8)) M2 (.A(Da[25:2]), .sel(1'b1), .D(M2_d));
  ROM #(.AddrBits(24), .Bits(8)) M3 (.A(Da[25:2]), .sel(1'b1), .D(M3_d));
  ROM #(.AddrBits(24), .Bits(8)) M4 (.A(Da[25:2]), .sel(1'b1), .D(M4_d));
  Multiplexer #(.Selector_Bits(2), .Bits(32)) multiplexer_1 (
    .sel(Da[1:0]), .in_0({M1_d, M2_d, M3_d, M4_d}), .in_1({M2_d, M3_d, M4_d, M1_d}),
    .in_2({M3_d, M4_d, M1_d, M2_d}), .in_3({M4_d, M1_d, M2_d, M3_d}), .out(Instr));

  // Notes on the sheet:
  //   contents of M1 (hex, n*v repeats v):
  //   1
  //   contents of M2 (hex, n*v repeats v):
  //   0,20,53
  //   contents of M3 (hex, n*v repeats v):
  //   2,3,3
  //   contents of M4 (hex, n*v repeats v):
  //   93,13,b3
endmodule
