// Digital circuit Memoria.dig as structural Verilog
module Memoria (
  input  [31:0] addr,
  input  [31:0] DataW,
  input  WE,
  input  [2:0] DMCtrl,
  input  clk,
  output [31:0] DataR
);

  wire [7:0] multiplexer_1_out, multiplexer_2_out, multiplexer_3_out, multiplexer_4_out, multiplexer_5_out,
       multiplexer_6_out, multiplexer_7_out, multiplexer_8_out, R1_d, R2_d, R3_d, R4_d;
  wire [31:0] bitextender_1_out, bitextender_2_out, notconnected_1_out, notconnected_2_out,
       notconnected_3_out;

  Multiplexer #(.Selector_Bits(2), .Bits(8)) multiplexer_1 (
    .sel(addr[1:0]), .in_0(DataW[31:24]), .in_1(DataW[7:0]), .in_2(DataW[15:8]), .in_3(DataW[23:16]),
    .out(multiplexer_1_out));
  BlockRAMDualPort #(.AddrBits(24), .Bits(8)) R1 (.A(addr[25:2]), .Din(multiplexer_1_out), .str(WE), .C(clk), .D(R1_d));
  Multiplexer #(.Selector_Bits(2), .Bits(8)) multiplexer_2 (
    .sel(addr[1:0]), .in_0(DataW[23:16]), .in_1(DataW[31:24]), .in_2(DataW[7:0]), .in_3(DataW[15:8]),
    .out(multiplexer_2_out));
  BlockRAMDualPort #(.AddrBits(24), .Bits(8)) R2 (.A(addr[25:2]), .Din(multiplexer_2_out), .str(WE), .C(clk), .D(R2_d));
  Multiplexer #(.Selector_Bits(2), .Bits(8)) multiplexer_3 (
    .sel(addr[1:0]), .in_0(R1_d), .in_1(R2_d), .in_2(R3_d), .in_3(R4_d), .out(multiplexer_3_out));
  Multiplexer #(.Selector_Bits(2), .Bits(8)) multiplexer_4 (
    .sel(addr[1:0]), .in_0(DataW[15:8]), .in_1(DataW[23:16]), .in_2(DataW[31:24]), .in_3(DataW[7:0]),
    .out(multiplexer_4_out));
  BlockRAMDualPort #(.AddrBits(24), .Bits(8)) R3 (.A(addr[25:2]), .Din(multiplexer_4_out), .str(WE), .C(clk), .D(R3_d));
  Multiplexer #(.Selector_Bits(2), .Bits(8)) multiplexer_5 (
    .sel(addr[1:0]), .in_0(R2_d), .in_1(R3_d), .in_2(R4_d), .in_3(R1_d), .out(multiplexer_5_out));
  Multiplexer #(.Selector_Bits(2), .Bits(8)) multiplexer_6 (
    .sel(addr[1:0]), .in_0(R3_d), .in_1(R4_d), .in_2(R1_d), .in_3(R2_d), .out(multiplexer_6_out));
  Multiplexer #(.Selector_Bits(2), .Bits(8)) multiplexer_7 (
    .sel(addr[1:0]), .in_0(DataW[7:0]), .in_1(DataW[15:8]), .in_2(DataW[23:16]), .in_3(DataW[31:24]),
    .out(multiplexer_7_out));
  BlockRAMDualPort #(.AddrBits(24), .Bits(8)) R4 (.A(addr[25:2]), .Din(multiplexer_7_out), .str(WE), .C(clk), .D(R4_d));
  Multiplexer #(.Selector_Bits(2), .Bits(8)) multiplexer_8 (
    .sel(addr[1:0]), .in_0(R4_d), .in_1(R1_d), .in_2(R2_d), .in_3(R3_d), .out(multiplexer_8_out));
  BitExtender #(.outputBits(32)) bitextender_1 (.in(multiplexer_3_out), .out(bitextender_1_out));
  BitExtender #(.inputBits(16), .outputBits(32)) bitextender_2 (
    .in({multiplexer_3_out, multiplexer_5_out}), .out(bitextender_2_out));
  Multiplexer #(.Selector_Bits(3), .Bits(32)) multiplexer_9 (
    .sel(DMCtrl), .in_0(bitextender_1_out), .in_1(bitextender_2_out),
    .in_2({multiplexer_3_out, multiplexer_5_out, multiplexer_6_out, multiplexer_8_out}),
    .in_3({{24{1'b0}}, multiplexer_3_out}), .in_4({{16{1'b0}}, multiplexer_3_out, multiplexer_5_out}),
    .in_5(notconnected_1_out), .in_6(notconnected_2_out), .in_7(notconnected_3_out), .out(DataR));
  // NotConnected on notconnected_1_out
  // NotConnected on notconnected_2_out
  // NotConnected on notconnected_3_out
endmodule
