// Digital circuit RISC-V.dig as structural Verilog
module RISC_V (
  input  clk,
  output [31:0] out_2,
  output [31:0] out_3
);

  wire ALUASrc, ALUBSrc, branch_unit_1_nxtpcsrc, DMWr, not_1_out, RUWE;
  wire [1:0] RUWrSrc;
  wire [2:0] DMCtrl, immSrc, inst_decoder_1_p3;
  wire [3:0] ALUOp;
  wire [4:0] cu_1_brop, inst_decoder_1_p5, inst_decoder_1_p6, inst_decoder_1_p7;
  wire [6:0] inst_decoder_1_p2, inst_decoder_1_p4;
  wire [24:0] inst_decoder_1_p8;
  wire [31:0] add_1_s, calu_1_p4, immgen_1_imm_ext, multiplexer_1_out, multiplexer_2_out, multiplexer_3_out,
       multiplexer_4_out, notconnected_1_out, PC_q, RU_da, RU_db;

  not not_1 (not_1_out, clk);
  Register #(.Bits(32), .isProgramCounter("true")) PC (.D(multiplexer_3_out), .C(not_1_out), .en(1'b1), .Q(PC_q));
  InsMem insmem_1 (.Da(PC_q[25:0]), .Instr(out_2));
  // Inst_Decoder inst_decoder_1: pin names not known; wires that end beside it: out_2, inst_decoder_1_p2, inst_decoder_1_p3, inst_decoder_1_p4, inst_decoder_1_p5, inst_decoder_1_p6, inst_decoder_1_p7, inst_decoder_1_p8
  Add #(.Bits(32)) add_1 (.a(32'h4), .b(PC_q), .c_i(1'b0), .s(add_1_s));  // open: c_o
  CU cu_1 (
    .OpCode(inst_decoder_1_p2), .func3(inst_decoder_1_p3), .func7(inst_decoder_1_p4), .RUWE(RUWE),
    .immSrc(immSrc), .ALUASrc(ALUASrc), .ALUBSrc(ALUBSrc), .DMWr(DMWr), .DMCtrl(DMCtrl), .RUWrSrc(RUWrSrc),
    .ALUOp(ALUOp), .BrOp(cu_1_brop));
  immGen immgen_1 (.imm(inst_decoder_1_p8), .immSrc(immSrc), .imm_Ext(immgen_1_imm_ext));
  RegisterFile #(.AddrBits(5), .Bits(32)) RU (
    .Din(multiplexer_4_out), .we(RUWE), .Rw(inst_decoder_1_p5), .C(clk), .Ra(inst_decoder_1_p6),
    .Rb(inst_decoder_1_p7), .Da(RU_da), .Db(RU_db));
  Multiplexer #(.Bits(32)) multiplexer_1 (.sel(ALUASrc), .in_0(RU_da), .in_1(PC_q), .out(multiplexer_1_out));
  Multiplexer #(.Bits(32)) multiplexer_2 (
    .sel(ALUBSrc), .in_0(RU_db), .in_1(immgen_1_imm_ext), .out(multiplexer_2_out));
  Branch_Unit branch_unit_1 (.A(RU_da), .B(RU_db), .BrOp(cu_1_brop), .NxtPCSrc(branch_unit_1_nxtpcsrc));
  // cALU calu_1: pin names not known; wires that end beside it: ALUOp, multiplexer_1_out, multiplexer_2_out, calu_1_p4
  Multiplexer #(.Bits(32)) multiplexer_3 (
    .sel(branch_unit_1_nxtpcsrc), .in_0(add_1_s), .in_1(calu_1_p4), .out(multiplexer_3_out));
  Memoria memoria_1 (.addr(calu_1_p4), .DataW(RU_db), .WE(DMWr), .DMCtrl(DMCtrl), .clk(clk), .DataR(out_3));
  // NotConnected on notconnected_1_out
  Multiplexer #(.Selector_Bits(2), .Bits(32)) multiplexer_4 (
    .sel(RUWrSrc), .in_0(calu_1_p4), .in_1(out_3), .in_2(add_1_s), .in_3(notconnected_1_out),
    .out(multiplexer_4_out));
endmodule
